# Fritzing sketch schematic (saved by Fritzing 0.9.10b)

parts:
  M1 = ESP32-S3-DevKitC-1-N8R8-v1 [part_number=ESP32-S3-DevKitC-1-N8R8-v1]
  Pololu_A1 = Pololu A4988 [package=SO16]
  M2 = Stepper Motor - Bipolar
  RE2 = KY-040 Rotary encoder [package=THT]
  A1 = WMYCONGCONG buck converter
  C1 = Capacitor Polarized [package=panasonic_c]
  JACK1 = 2.1mm Barrel Jack with Terminal Block

nets:
  N1: M1.pin_1, RE2.Vcc
  N2: M1.pin_21, Pololu_A1.VDD, A1.Pin_4
  GND: M1.pin_22, M1.pin_23, M1.pin_24, M1.pin_44, Pololu_A1.GND, RE2.GND, A1.Pin_3, C1.-, JACK1.NEG
  N3: M1.pin_36, Pololu_A1.STEP
  N4: M1.pin_37, Pololu_A1.DIR
  N5: M1.pin_38, RE2.CLK
  N6: M1.pin_39, RE2.DT
  N7: M1.pin_40, RE2.SW
  N8: Pololu_A1.1B, M2.D
  N9: Pololu_A1.1A, M2.B
  N10: Pololu_A1.2A, M2.C
  N11: Pololu_A1.2B, M2.A
  N12: Pololu_A1.VMOT, A1.Pin_2
  N13: C1.+, JACK1.POS

notes:
  CLK - IO2
  DT - IO42
  SW - IO41
  STEP - IO39
  DIR - IO40
  12V
  5V
  3V3
  GND

custom parts:
  ESP32-S3-DevKitC-1-N8R8-v1: ESP32-S3-DevKitC-1-N8R8-v1 This module is 44pins long (2x22) and 11 pins width.
  KY-040 Rotary encoder: KY-040 Rotary Encoder with switch on breakout borad from AZ Delivery
  WMYCONGCONG buck converter: These amazing little DC-DC converters feature a wide input voltage of 4.5-24V and the output voltage can be set to one of six fixed voltages, or fully variable, just by bridging the relevant solder pads on the back of the PCB..
